# Fritzing sketch MIDTERM2 (saved by Fritzing 0.9.4)
breadboards: 1

parts:
  Argon1 = Particle Argon
  OLED = Grove OLED 128x96
  SENS1 = SoilWatch 10
  M1 = BMP280
  AIR_QUALITY_SENSOR = MQ-131 breakout
  DUST_SENSOR = Grove Dust Sensor
  Relay1 = Relay - 6 pins [package="DIP (Dual Inline) [THT]"]
  Q1 = PNP-Transistor [package="SOT-23 [SMD]"]
  R1 = Resistor [tolerance=±5% resistance=220 package="2512 [SMD]"]
  R2 = Resistor [tolerance=±5% resistance=2.2k package="2512 [SMD]"]
  PUMP = DC Motor

nets:
  VCC: Argon1.3.3V, OLED.VCC, SENS1.VCC, M1.VIN
  GND: Argon1.GND, OLED.GND, SENS1.GND, M1.GND, AIR_QUALITY_SENSOR.GND, DUST_SENSOR.GND, Relay1.GND, Q1.1, R2.Pin_1, PUMP.pin_2
  N1: Argon1.A0, SENS1.OUT
  N2: Argon1.A1, AIR_QUALITY_SENSOR.AO
  N3: Argon1.SDA, OLED.SDA, M1.SDA
  N4: Argon1.SCL, OLED.SCL, M1.SCL
  N5: Argon1.D2, Q1.0, R2.Pin_0
  N6: Argon1.D3, DUST_SENSOR.SIG
  VCC_2: Argon1.VUSB, AIR_QUALITY_SENSOR.VCC, DUST_SENSOR.VCC, Relay1.COM, R1.Pin_0
  N7: Relay1.VCC, Q1.2, R1.Pin_1
  N8: Relay1.ON, PUMP.pin_1

custom parts:
  Particle Argon: The Argon is a powerful Wi-Fi enabled development board that can act as either a standalone Wi-Fi endpoint or Wi-Fi enabled gateway for Particle Mesh networks. It is based on the Nordic nRF52840 and has built-in battery charging circuitry so it’s easy to connect a Li-Po and deploy your local network in minutes. The Argon is great for connecting existing projects to the Particle Device Cloud or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
  SoilWatch 10: SoilWatch 10 - Capacitive soil moisture sensor
  BMP280: Temperature Humidity Barometric presure Sensor, I2C
  MQ-131 breakout: SKU: 101282
  Grove Dust Sensor: PPD42 Grove Dust Sensor
  Relay - 6 pins: A DIP stand-in part for whatever IC you want. With 6 pins on a 900mil dual inline package (DIP) footprint.
